// Digital circuit EEPROM.dig as structural Verilog
module EEPROM (
  input  a__c,
  input  clk,
  output o0,
  output o1,
  output o2,
  output o3,
  output o4,
  output o5,
  output o6,
  output o7,
  output [1:0] error_count
);

  wire a, ad, and_1_out, and_2_out, and_3_out, and_4_out, and_5_out, and_6_out, and_7_out, and_8_out,
       and_9_out, and_10_out, and_11_out, and_12_out, and_13_out, and_14_out, and_15_out, and_16_out,
       and_17_out, and_18_out, and_19_out, and_21_out, and_22_out, b, B_q, c, comparator_1_eq,
       comparator_2_eq, counter_1_ovf, counterpreset_3_ovf, counterpreset_5_ovf, d_ff_1_nq, d_ff_1_q,
       d_ff_as_9_q, delay_1_out, delay_2_out, delay_3_out, delay_4_out, delay_5_out, delay_6_out, Enter_out,
       in, jk_ff_1_q, jk_ff_as_1_q, jk_ff_as_2_nq, jk_ff_as_2_q, jk_ff_as_4_q, Lock_out, monoflop_1_q,
       multiplexer_1_out, multiplexer_2_out, multiplexer_3_out, multiplexer_4_out, multiplexer_5_out, no,
       nor_1_out, nor_3_out, nor_4_out, not_1_out, not_2_out, not_3_out, not_4_out, not_5_out, not_6_out,
       not_7_out, not_8_out, not_9_out, not_10_out, or_1_out, or_2_out, or_3_out, or_4_out, or_5_out,
       or_6_out, or_7_out, or_8_out, pr, PR_2_nq, PR_out, rs_ff_as_1_nq, rs_ff_as_1_q, rs_ff_as_2_nq,
       rs_ff_as_2_q, rs_ff_as_3_q, rs_ff_as_4_nq, rst, t_ff_1_q, turn_out, us, WD_out, xor_1_out, xor_2_out,
       xor_3_out;
  wire [3:0] counterpreset_1_out, counterpreset_2_out, counterpreset_3_out, counterpreset_4_out,
       counterpreset_5_out;
  wire [7:0] eeprom_1_d, pass;

  Button turn (.out(turn_out));
  T_FF u_B (.T(1'b1), .C(turn_out), .Q(B_q));  // open: nQ
  T_FF t_ff_1 (.T(1'b1), .C(turn_out), .Q(t_ff_1_q));  // open: nQ
  nor nor_1 (nor_1_out, a, c);
  Delay #(.delayTime(20)) delay_1 (.in(B_q), .out(delay_1_out));
  Delay #(.delayTime(20)) delay_2 (.in(t_ff_1_q), .out(delay_2_out));
  Button Enter (.out(Enter_out));
  and and_1 (and_1_out, Enter_out, nor_1_out);
  Multiplexer multiplexer_1 (.sel(a__c), .in_0(B_q), .in_1(delay_1_out), .out(multiplexer_1_out));
  Multiplexer multiplexer_2 (.sel(a__c), .in_0(delay_2_out), .in_1(t_ff_1_q), .out(multiplexer_2_out));
  Button POR_RST (.out(rst));
  xor xor_1 (xor_1_out, multiplexer_1_out, multiplexer_2_out);
  Multiplexer multiplexer_3 (.sel(rst), .in_0(1'b0), .in_1(multiplexer_2_out), .out(multiplexer_3_out));
  or or_1 (or_1_out, rst, and_1_out);
  not not_1 (not_1_out, multiplexer_2_out);
  not not_2 (not_2_out, b);
  or or_2 (or_2_out, rst, d_ff_as_9_q);
  Multiplexer multiplexer_4 (.sel(rst), .in_0(1'b0), .in_1(not_1_out), .out(multiplexer_4_out));
  and and_2 (and_2_out, not_2_out, and_1_out);
  JK_FF_AS jk_ff_as_1 (
    .Set(multiplexer_3_out), .J(1'b1), .C(~xor_1_out), .K(1'b1), .Clr(multiplexer_4_out), .Q(jk_ff_as_1_q));  // open: nQ
  xor xor_2 (xor_2_out, multiplexer_1_out, jk_ff_as_1_q);
  xor xor_3 (xor_3_out, jk_ff_as_1_q, multiplexer_2_out);
  JK_FF_AS jk_ff_as_2 (
    .Set(1'b0), .J(1'b1), .C(~and_2_out), .K(1'b1), .Clr(or_2_out), .Q(jk_ff_as_2_q), .nQ(jk_ff_as_2_nq));
  nor nor_2 (no, a, b, c);
  nor nor_3 (nor_3_out, 1'b0, xor_2_out, xor_3_out);
  and and_3 (and_3_out, xor_2_out, rs_ff_as_2_nq);
  and and_4 (and_4_out, rs_ff_as_1_nq, xor_3_out);
  not not_3 (not_3_out, delay_3_out);
  Delay #(.delayTime(20)) delay_3 (.in(or_1_out), .out(delay_3_out));
  JK_FF_AS jk_ff_as_3 (.Set(1'b0), .J(1'b1), .C(jk_ff_as_2_nq), .K(1'b1), .Clr(or_2_out), .Q(b));  // open: nQ
  and and_5 (and_5_out, xor_1_out, no);
  and and_6 (and_6_out, or_1_out, not_3_out);
  RS_FF_AS rs_ff_as_1 (.S(and_3_out), .R(nor_3_out), .Q(rs_ff_as_1_q), .nQ(rs_ff_as_1_nq));
  RS_FF_AS rs_ff_as_2 (.S(and_4_out), .R(nor_3_out), .Q(rs_ff_as_2_q), .nQ(rs_ff_as_2_nq));
  JK_FF_AS jk_ff_as_4 (.Set(1'b0), .J(b), .C(and_1_out), .K(b), .Clr(or_2_out), .Q(jk_ff_as_4_q));  // open: nQ
  RS_FF_AS rs_ff_as_3 (.S(rs_ff_as_1_q), .R(rs_ff_as_2_q), .Q(rs_ff_as_3_q));  // open: nQ
  Multiplexer multiplexer_5 (.sel(or_1_out), .in_0(and_5_out), .in_1(and_6_out), .out(multiplexer_5_out));
  Seven_Seg_Hex seven_seg_hex_1 (.d(counterpreset_1_out), .dp(1'b0));
  CounterPreset #(.maxValue(15), .Bits(4)) counterpreset_1 (
    .en(1'b1), .C(~multiplexer_5_out), .dir(rs_ff_as_3_q), .in(4'b0000), .ld(1'b0), .clr(or_1_out),
    .out(counterpreset_1_out));  // open: ovf
  not not_4 (not_4_out, jk_ff_as_2_q);
  and and_7 (and_7_out, jk_ff_as_2_q, and_2_out);
  and and_8 (and_8_out, and_2_out, not_4_out);
  D_FF_AS d_ff_as_1 (.Set(1'b0), .D(counterpreset_1_out[0]), .C(and_8_out), .Clr(or_2_out), .Q(o0));  // open: nQ
  D_FF_AS d_ff_as_2 (.Set(1'b0), .D(counterpreset_1_out[1]), .C(and_8_out), .Clr(or_2_out), .Q(o1));  // open: nQ
  D_FF_AS d_ff_as_3 (.Set(1'b0), .D(counterpreset_1_out[2]), .C(and_8_out), .Clr(or_2_out), .Q(o2));  // open: nQ
  D_FF_AS d_ff_as_4 (.Set(1'b0), .D(counterpreset_1_out[3]), .C(and_8_out), .Clr(or_2_out), .Q(o3));  // open: nQ
  D_FF_AS d_ff_as_5 (.Set(1'b0), .D(counterpreset_1_out[0]), .C(and_7_out), .Clr(or_2_out), .Q(o4));  // open: nQ
  D_FF_AS d_ff_as_6 (.Set(1'b0), .D(counterpreset_1_out[1]), .C(and_7_out), .Clr(or_2_out), .Q(o5));  // open: nQ
  D_FF_AS d_ff_as_7 (.Set(1'b0), .D(counterpreset_1_out[2]), .C(and_7_out), .Clr(or_2_out), .Q(o6));  // open: nQ
  D_FF_AS d_ff_as_8 (.Set(1'b0), .D(counterpreset_1_out[3]), .C(and_7_out), .Clr(or_2_out), .Q(o7));  // open: nQ
  Register #(.Bits(8)) register_1 (.D({o7, o6, o5, o4, o3, o2, o1, o0}), .C(jk_ff_as_4_q), .en(1'b1), .Q(pass));
  Seven_Seg_Hex seven_seg_hex_2 (.d({o7, o6, o5, o4}), .dp(1'b0));
  Seven_Seg_Hex seven_seg_hex_3 (.d({o3, o2, o1, o0}), .dp(1'b0));
  Comparator #(.Bits(8)) comparator_1 (
    .a({o7, o6, o5, o4, o3, o2, o1, o0}), .b(pass), .eq(comparator_1_eq));  // open: gt, lt
  and and_9 (and_9_out, comparator_1_eq, jk_ff_as_4_q);
  D_FF_AS d_ff_as_9 (.Set(1'b0), .D(and_9_out), .C(clk), .Clr(rst), .Q(d_ff_as_9_q));  // open: nQ
  and and_10 (and_10_out, ~pr, ad);  // And
  not not_5 (not_5_out, delay_4_out);
  Delay #(.delayTime(5)) delay_4 (.in(and_17_out), .out(delay_4_out));
  JK_FF jk_ff_1 (.J(in), .C(clk), .K(us), .Q(jk_ff_1_q));  // open: nQ
  Button Lock (.out(Lock_out));
  and and_11 (and_11_out, d_ff_as_9_q, pr);
  and and_12 (and_12_out, ~in, clk);  // And
  and and_13 (and_13_out, not_6_out, clk);
  not not_6 (not_6_out, counterpreset_3_ovf);
  and and_14 (and_14_out, not_5_out, and_17_out);
  or or_3 (or_3_out, jk_ff_1_q, rst, Lock_out);
  Button u_PR (.out(PR_out));
  Monoflop #(.timerDelay(10)) monoflop_1 (.C(and_11_out), .R(rst), .Q(monoflop_1_q));  // open: nQ
  RS_FF_AS rs_ff_as_4 (.S(pr), .R(or_5_out), .nQ(rs_ff_as_4_nq));  // open: Q
  CounterPreset #(.maxValue(15), .Bits(4)) counterpreset_2 (
    .en(and_10_out), .C(and_12_out), .dir(1'b1), .in(4'b1000), .ld(us), .clr(1'b0),
    .out(counterpreset_2_out), .ovf(in));
  or or_4 (or_4_out, and_13_out, and_14_out);
  Seven_Seg_Hex seven_seg_hex_4 (.d(counterpreset_2_out), .dp(1'b0));
  Button WD (.out(WD_out));
  not not_7 (not_7_out, rst);
  CounterPreset #(.maxValue(6), .Bits(4)) counterpreset_3 (
    .en(1'b1), .C(or_4_out), .dir(1'b1), .in(4'b0101), .ld(and_17_out), .clr(rst), .out(counterpreset_3_out),
    .ovf(counterpreset_3_ovf));
  RS_FF_AS A_nU (.S(and_16_out), .R(or_3_out), .Q(ad), .nQ(us));
  or or_5 (or_5_out, rst, rst, WD_out);
  EEPROM #(.AddrBits(8), .Bits(8)) eeprom_1 (
    .A({8{1'b0}}), .CS(not_7_out), .WE(monoflop_1_q), .OE(rs_ff_as_4_nq), .D(eeprom_1_d));
  assign eeprom_1_d = pr ? pass : 8'bz;  // Driver driver_1
  LED led_1 (.in(counterpreset_3_out[0]));
  and and_15 (and_15_out, PR_out, ad);
  LED led_2 (.in(ad));
  LED led_3 (.in(us));
  or or_6 (or_6_out, rst, ad, counterpreset_4_out[1]);
  Comparator #(.Bits(8)) comparator_2 (.a(pass), .b(eeprom_1_d), .eq(comparator_2_eq));  // open: gt, lt
  Delay #(.delayTime(5)) delay_5 (.in(or_6_out), .out(delay_5_out));
  RS_FF_AS PR_2 (.S(and_15_out), .R(or_5_out), .Q(pr), .nQ(PR_2_nq));
  not not_8 (not_8_out, delay_5_out);
  and and_16 (and_16_out, d_ff_as_9_q, comparator_2_eq);
  and and_17 (and_17_out, d_ff_as_9_q, ~comparator_2_eq);  // And
  and and_18 (and_18_out, not_8_out, or_6_out);
  or or_7 (or_7_out, and_17_out, and_18_out);
  or or_8 (or_8_out, rst, ad, counterpreset_4_out[1]);
  and and_19 (and_19_out, d_ff_1_nq, pr);
  Counter #(.Bits(2)) counter_1 (.en(1'b1), .C(or_7_out), .clr(or_8_out), .out(error_count), .ovf(counter_1_ovf));
  D_FF d_ff_1 (.D(and_19_out), .C(clk), .Q(d_ff_1_q), .nQ(d_ff_1_nq));
  and and_20 (a, PR_2_nq, ad);
  and and_21 (and_21_out, c, clk);
  Delay #(.delayTime(5)) delay_6 (.in(counter_1_ovf), .out(delay_6_out));
  LED led_4 (.in(d_ff_1_q));
  not not_9 (not_9_out, delay_6_out);
  and and_22 (and_22_out, not_9_out, counter_1_ovf);
  CounterPreset #(.maxValue(9), .Bits(4)) counterpreset_4 (
    .en(1'b1), .C(and_21_out), .dir(1'b1), .in(4'b0000), .ld(and_22_out), .clr(1'b0),
    .out(counterpreset_4_out));  // open: ovf
  Seven_Seg_Hex seven_seg_hex_5 (.d(counterpreset_5_out), .dp(1'b0));
  Seven_Seg_Hex seven_seg_hex_6 (.d(counterpreset_4_out), .dp(1'b0));
  CounterPreset #(.maxValue(15), .Bits(4)) counterpreset_5 (
    .en(nor_4_out), .C(and_21_out), .dir(1'b1), .in(4'b0011), .ld(and_22_out), .clr(1'b0),
    .out(counterpreset_5_out), .ovf(counterpreset_5_ovf));
  not not_10 (not_10_out, and_22_out);
  // And and_23 has open pins: In_1=counterpreset_4_out[3], In_2=counterpreset_4_out[0], out=open
  nor nor_4 (nor_4_out, counterpreset_4_out[0], counterpreset_4_out[1], counterpreset_4_out[2], counterpreset_4_out[3]);
  nand nand_1 (c, nor_4_out, not_10_out, counterpreset_5_ovf);

  // Notes on the sheet:
  //   a__c: default 1
  //   Encoder
  //   Sim-only
  //   contents of eeprom_1 (hex, n*v repeats v):
  //   0,0,f,7*0,c
endmodule
