// Digital circuit encoder.dig as structural Verilog
module encoder (
  input  a__c,
  output o0,
  output o1,
  output o2,
  output o3,
  output o4,
  output o5,
  output o6,
  output o7,
  output to_EEPROM_WE,
  output [7:0] pass
);

  wire and_1_out, and_2_out, and_3_out, and_4_out, and_5_out, and_6_out, and_7_out, comparator_1_eq,
       delay_1_out, delay_2_out, delay_3_out, delay_4_out, driver_1_out, driver_2_out, driverinvsel_3_out,
       Enter_out, jk_ff_as_1_q, jk_ff_as_2_q, jk_ff_as_3_q, jk_ff_as_4_nq, jk_ff_as_4_q, jk_ff_as_5_q,
       multiplexer_1_out, multiplexer_2_out, nor_1_out, not_1_out, not_2_out, not_3_out, not_4_out,
       not_5_out, not_6_out, not_7_out, or_1_out, or_2_out, or_3_out, POR_RST_out, rs_ff_as_1_q, t_ff_1_q,
       t_ff_2_q, turn_out, xor_1_out, xor_2_out, xor_3_out;
  wire [3:0] counterpreset_1_out, demultiplexer_1_out_0, demultiplexer_1_out_1;

  Delay delay_1 (.in(Enter_out), .out(delay_1_out));
  not not_1 (not_1_out, delay_1_out);
  Button turn (.out(turn_out));
  nor nor_1 (nor_1_out, Enter_out, not_1_out);
  T_FF t_ff_1 (.T(1'b1), .C(turn_out), .Q(t_ff_1_q));  // open: nQ
  T_FF t_ff_2 (.T(1'b1), .C(turn_out), .Q(t_ff_2_q));  // open: nQ
  or or_1 (or_1_out, and_7_out, nor_1_out);
  Delay #(.delayTime(20)) delay_2 (.in(t_ff_1_q), .out(delay_2_out));
  Delay #(.delayTime(20)) delay_3 (.in(t_ff_2_q), .out(delay_3_out));
  Multiplexer multiplexer_1 (.sel(a__c), .in_0(t_ff_1_q), .in_1(delay_2_out), .out(multiplexer_1_out));
  Multiplexer multiplexer_2 (.sel(a__c), .in_0(delay_3_out), .in_1(t_ff_2_q), .out(multiplexer_2_out));
  Button POR_RST (.out(POR_RST_out));
  Button Enter (.out(Enter_out));
  JK_FF_AS jk_ff_as_1 (
    .Set(1'b0), .J(to_EEPROM_WE), .C(or_1_out), .K(to_EEPROM_WE), .Clr(or_3_out), .Q(jk_ff_as_1_q));  // open: nQ
  not not_2 (not_2_out, multiplexer_2_out);
  or or_2 (or_2_out, POR_RST_out, Enter_out);
  JK_FF_AS jk_ff_as_2 (
    .Set(1'b0), .J(jk_ff_as_1_q), .C(or_1_out), .K(jk_ff_as_1_q), .Clr(or_3_out), .Q(jk_ff_as_2_q));  // open: nQ
  xor xor_1 (xor_1_out, multiplexer_1_out, multiplexer_2_out);
  assign driver_1_out = or_2_out ? not_2_out : 1'bz;  // Driver driver_1
  assign driver_2_out = or_2_out ? multiplexer_2_out : 1'bz;  // Driver driver_2
  not not_3 (not_3_out, jk_ff_as_5_q);
  or or_3 (or_3_out, POR_RST_out, jk_ff_as_2_q);
  and and_1 (and_1_out, not_3_out, Enter_out);
  JK_FF_AS jk_ff_as_3 (
    .Set(driver_2_out), .J(1'b1), .C(~xor_1_out), .K(1'b1), .Clr(driver_1_out), .Q(jk_ff_as_3_q));  // open: nQ
  assign driver_1_out = ~or_2_out ? 1'b0 : 1'bz;  // DriverInvSel driverinvsel_1
  assign driver_2_out = ~or_2_out ? 1'b0 : 1'bz;  // DriverInvSel driverinvsel_2
  xor xor_2 (xor_2_out, multiplexer_1_out, jk_ff_as_3_q);
  xor xor_3 (xor_3_out, jk_ff_as_3_q, multiplexer_2_out);
  JK_FF_AS jk_ff_as_4 (
    .Set(1'b0), .J(1'b1), .C(~and_1_out), .K(1'b1), .Clr(or_3_out), .Q(jk_ff_as_4_q), .nQ(jk_ff_as_4_nq));
  not not_4 (not_4_out, xor_3_out);
  not not_5 (not_5_out, xor_2_out);
  Delay #(.delayTime(20)) delay_4 (.in(or_2_out), .out(delay_4_out));
  JK_FF_AS jk_ff_as_5 (
    .Set(1'b0), .J(1'b1), .C(jk_ff_as_4_nq), .K(1'b1), .Clr(or_3_out), .Q(jk_ff_as_5_q));  // open: nQ
  and and_2 (and_2_out, xor_2_out, not_4_out);
  and and_3 (and_3_out, not_5_out, xor_3_out);
  and and_4 (and_4_out, or_2_out, not_6_out);
  not not_6 (not_6_out, delay_4_out);
  JK_FF_AS jk_ff_as_6 (
    .Set(1'b0), .J(jk_ff_as_5_q), .C(Enter_out), .K(jk_ff_as_5_q), .Clr(or_3_out), .Q(to_EEPROM_WE));  // open: nQ
  RS_FF_AS rs_ff_as_1 (.S(and_2_out), .R(and_3_out), .Q(rs_ff_as_1_q));  // open: nQ
  assign driverinvsel_3_out = ~or_2_out ? xor_1_out : 1'bz;  // DriverInvSel driverinvsel_3
  assign driverinvsel_3_out = or_2_out ? and_4_out : 1'bz;  // Driver driver_3
  CounterPreset #(.maxValue(15), .Bits(4)) counterpreset_1 (
    .en(1'b1), .C(~driverinvsel_3_out), .dir(rs_ff_as_1_q), .in(4'b0000), .ld(1'b0), .clr(or_2_out),
    .out(counterpreset_1_out));  // open: ovf
  Demultiplexer #(.Bits(4)) demultiplexer_1 (
    .sel(jk_ff_as_4_q), .in(counterpreset_1_out), .out_0(demultiplexer_1_out_0), .out_1(demultiplexer_1_out_1));
  not not_7 (not_7_out, jk_ff_as_4_q);
  and and_5 (and_5_out, jk_ff_as_4_q, and_1_out);
  and and_6 (and_6_out, and_1_out, not_7_out);
  D_FF_AS d_ff_as_1 (.Set(1'b0), .D(demultiplexer_1_out_0[0]), .C(and_6_out), .Clr(and_7_out), .Q(o0));  // open: nQ
  D_FF_AS d_ff_as_2 (.Set(1'b0), .D(demultiplexer_1_out_0[1]), .C(and_6_out), .Clr(and_7_out), .Q(o1));  // open: nQ
  D_FF_AS d_ff_as_3 (.Set(1'b0), .D(demultiplexer_1_out_0[2]), .C(and_6_out), .Clr(and_7_out), .Q(o2));  // open: nQ
  D_FF_AS d_ff_as_4 (.Set(1'b0), .D(demultiplexer_1_out_0[3]), .C(and_6_out), .Clr(and_7_out), .Q(o3));  // open: nQ
  D_FF_AS d_ff_as_5 (.Set(1'b0), .D(demultiplexer_1_out_1[0]), .C(and_5_out), .Clr(and_7_out), .Q(o4));  // open: nQ
  D_FF_AS d_ff_as_6 (.Set(1'b0), .D(demultiplexer_1_out_1[1]), .C(and_5_out), .Clr(and_7_out), .Q(o5));  // open: nQ
  D_FF_AS d_ff_as_7 (.Set(1'b0), .D(demultiplexer_1_out_1[2]), .C(and_5_out), .Clr(and_7_out), .Q(o6));  // open: nQ
  D_FF_AS d_ff_as_8 (.Set(1'b0), .D(demultiplexer_1_out_1[3]), .C(and_5_out), .Clr(and_7_out), .Q(o7));  // open: nQ
  Seven_Seg_Hex seven_seg_hex_1 (.d({o7, o6, o5, o4}), .dp(1'b0));
  Register #(.Bits(8)) register_1 (.D({o7, o6, o5, o4, o3, o2, o1, o0}), .C(to_EEPROM_WE), .en(1'b1), .Q(pass));
  Seven_Seg_Hex seven_seg_hex_2 (.d({o3, o2, o1, o0}), .dp(1'b0));
  Comparator #(.Bits(8)) comparator_1 (
    .a({o7, o6, o5, o4, o3, o2, o1, o0}), .b(pass), .eq(comparator_1_eq));  // open: gt, lt
  and and_7 (and_7_out, comparator_1_eq, to_EEPROM_WE);

  // Notes on the sheet:
  //   a__c: default 1
  //   Encoder
  //   Sim-only
endmodule
